# Fritzing sketch wiring (saved by Fritzing 0.8.7b)

parts:
  Raspberry_Pi_B_rev1 = Raspberry Pi B rev2
  SVert = Pushbutton [package="[THT]"]
  SRouge = Pushbutton [package="[THT]"]
  LCD1 = LCD screen  # not connected

nets:
  N1: Raspberry_Pi_B_rev1.GND, SVert.Pin_4, SRouge.Pin_1, SRouge.Pin_2
  N2: Raspberry_Pi_B_rev1.GPIO_23, SVert.Pin_2
  N3: Raspberry_Pi_B_rev1.GPIO_24, SRouge.Pin_3, SRouge.Pin_4

notes:
  GND
  VCC
  SDA
  SCL
  Green
  Red
